// Logisim project logic_power_switcher.circ as structural Verilog: 1 circuit, main circuit main
module main (
);

  wire d_ff_1_q, d_ff_2_q, d_ff_3_q, d_ff_4_q, d_ff_5_q, decoder_1_out1, decoder_1_out2, decoder_1_out3,
       decoder_1_out4, decoder_1_out5, dipswitch_1_sw4;
  wire [2:0] dipswitch_1_sw3;

  DipSwitch #(.number(4)) dipswitch_1 (
    .sw1(dipswitch_1_sw3[2]), .sw2(dipswitch_1_sw3[1]), .sw3(dipswitch_1_sw3[0]), .sw4(dipswitch_1_sw4));
  Decoder #(.enable("false"), .select(3)) decoder_1 (
    .out1(decoder_1_out1), .out2(decoder_1_out2), .out3(decoder_1_out3), .out4(decoder_1_out4),
    .out5(decoder_1_out5), .sel(dipswitch_1_sw3));  // open: out0, out6, out7
  D_Flip_Flop d_ff_1 (.D(dipswitch_1_sw4), .clk(decoder_1_out1), .Q(d_ff_1_q));  // open: Qn, preset, reset
  D_Flip_Flop d_ff_2 (.D(dipswitch_1_sw4), .clk(decoder_1_out2), .Q(d_ff_2_q));  // open: Qn, preset, reset
  D_Flip_Flop d_ff_3 (.D(dipswitch_1_sw4), .clk(decoder_1_out3), .Q(d_ff_3_q));  // open: Qn, preset, reset
  D_Flip_Flop d_ff_4 (.D(dipswitch_1_sw4), .clk(decoder_1_out4), .Q(d_ff_4_q));  // open: Qn, preset, reset
  D_Flip_Flop d_ff_5 (.D(dipswitch_1_sw4), .clk(decoder_1_out5), .Q(d_ff_5_q));  // open: Qn, preset, reset
  LED led_1 (.in(d_ff_1_q));
  LED led_2 (.in(d_ff_2_q));
  LED led_3 (.in(d_ff_3_q));
  LED led_4 (.in(d_ff_4_q));
  LED led_5 (.in(d_ff_5_q));
endmodule
