// Logisim project logic_power_switcher_2.circ as structural Verilog: 1 circuit, main circuit main
module main (
);

  wire button_1_out, dipswitch_2_sw1, n7400_1_pin2, n7400_1_pin3, n7400_1_pin5, n7400_1_pin6, n7400_1_pin11,
       n7400_1_pin13, n7400_2_pin2, n7400_2_pin3, n7400_2_pin5, n7400_2_pin6, n7400_2_pin11, n7400_2_pin13,
       n7400_3_pin2, n7400_3_pin3, n7400_3_pin5, n7400_3_pin6, n7400_3_pin11, n7400_3_pin13, n7400_4_pin2,
       n7400_4_pin3, n7400_4_pin5, n7400_4_pin6, n7400_4_pin11, n7400_4_pin13, n7400_5_pin2, n7400_5_pin3,
       n7400_5_pin5, n7400_5_pin6, n7400_5_pin11, n7400_5_pin13, n7400_6_pin2, n7400_6_pin3, n7400_6_pin5,
       n7400_6_pin6, n7400_6_pin11, n7400_6_pin13, n7400_7_pin2, n7400_7_pin3, n7400_7_pin5, n7400_7_pin6,
       n7400_7_pin11, n7400_7_pin13, n7400_8_pin2, n7400_8_pin3, n7400_8_pin5, n7400_8_pin6, n7400_8_pin11,
       n7400_8_pin13, n74138_1_pin1, n74138_1_pin2, n74138_1_pin3, n74138_1_pin4, n74138_1_pin6,
       n74138_1_pin7, n74138_1_pin9, n74138_1_pin10, n74138_1_pin11, n74138_1_pin12, n74138_1_pin13,
       n74138_1_pin14, n74138_1_pin15, n74377_1_pin1;

  _74138 u_74138_1 (
    .pin1(n74138_1_pin1), .pin2(n74138_1_pin2), .pin3(n74138_1_pin3), .pin4(n74138_1_pin4),
    .pin5(n74138_1_pin4), .pin6(n74138_1_pin6), .pin7(n74138_1_pin7), .pin15(n74138_1_pin15),
    .pin14(n74138_1_pin14), .pin13(n74138_1_pin13), .pin12(n74138_1_pin12), .pin11(n74138_1_pin11),
    .pin10(n74138_1_pin10), .pin9(n74138_1_pin9));
  DipSwitch #(.number(3)) dipswitch_1 (.sw1(n74138_1_pin3), .sw2(n74138_1_pin2), .sw3(n74138_1_pin1));
  LED led_1 (.in(n7400_1_pin2));
  LED led_2 (.in(n7400_2_pin2));
  LED led_3 (.in(n7400_3_pin2));
  LED led_4 (.in(n7400_4_pin2));
  LED led_5 (.in(n7400_5_pin2));
  LED led_6 (.in(n7400_6_pin2));
  LED led_7 (.in(n7400_7_pin2));
  Button button_1 (.out(button_1_out));
  LED led_8 (.in(n7400_8_pin2));
  DipSwitch #(.number(2)) dipswitch_2 (.sw1(dipswitch_2_sw1));  // open: sw2
  _7400 u_7400_1 (
    .pin1(n74138_1_pin15), .pin2(n7400_1_pin2), .pin3(n7400_1_pin3), .pin4(n7400_1_pin3),
    .pin5(n7400_1_pin5), .pin6(n7400_1_pin6), .pin13(n7400_1_pin13), .pin12(n74138_1_pin15),
    .pin11(n7400_1_pin11), .pin10(n7400_1_pin11), .pin9(dipswitch_2_sw1), .pin8(n7400_1_pin5));
  _7400 u_7400_2 (
    .pin1(n74138_1_pin14), .pin2(n7400_2_pin2), .pin3(n7400_2_pin3), .pin4(n7400_2_pin3),
    .pin5(n7400_2_pin5), .pin6(n7400_2_pin6), .pin13(n7400_2_pin13), .pin12(n74138_1_pin14),
    .pin11(n7400_2_pin11), .pin10(n7400_2_pin11), .pin9(dipswitch_2_sw1), .pin8(n7400_2_pin5));
  _7400 u_7400_3 (
    .pin1(n74138_1_pin13), .pin2(n7400_3_pin2), .pin3(n7400_3_pin3), .pin4(n7400_3_pin3),
    .pin5(n7400_3_pin5), .pin6(n7400_3_pin6), .pin13(n7400_3_pin13), .pin12(n74138_1_pin13),
    .pin11(n7400_3_pin11), .pin10(n7400_3_pin11), .pin9(dipswitch_2_sw1), .pin8(n7400_3_pin5));
  _7400 u_7400_4 (
    .pin1(n74138_1_pin12), .pin2(n7400_4_pin2), .pin3(n7400_4_pin3), .pin4(n7400_4_pin3),
    .pin5(n7400_4_pin5), .pin6(n7400_4_pin6), .pin13(n7400_4_pin13), .pin12(n74138_1_pin12),
    .pin11(n7400_4_pin11), .pin10(n7400_4_pin11), .pin9(dipswitch_2_sw1), .pin8(n7400_4_pin5));
  _7400 u_7400_5 (
    .pin1(n74138_1_pin11), .pin2(n7400_5_pin2), .pin3(n7400_5_pin3), .pin4(n7400_5_pin3),
    .pin5(n7400_5_pin5), .pin6(n7400_5_pin6), .pin13(n7400_5_pin13), .pin12(n74138_1_pin11),
    .pin11(n7400_5_pin11), .pin10(n7400_5_pin11), .pin9(dipswitch_2_sw1), .pin8(n7400_5_pin5));
  _7400 u_7400_6 (
    .pin1(n74138_1_pin10), .pin2(n7400_6_pin2), .pin3(n7400_6_pin3), .pin4(n7400_6_pin3),
    .pin5(n7400_6_pin5), .pin6(n7400_6_pin6), .pin13(n7400_6_pin13), .pin12(n74138_1_pin10),
    .pin11(n7400_6_pin11), .pin10(n7400_6_pin11), .pin9(dipswitch_2_sw1), .pin8(n7400_6_pin5));
  _7400 u_7400_7 (
    .pin1(n74138_1_pin9), .pin2(n7400_7_pin2), .pin3(n7400_7_pin3), .pin4(n7400_7_pin3), .pin5(n7400_7_pin5),
    .pin6(n7400_7_pin6), .pin13(n7400_7_pin13), .pin12(n74138_1_pin9), .pin11(n7400_7_pin11),
    .pin10(n7400_7_pin11), .pin9(dipswitch_2_sw1), .pin8(n7400_7_pin5));
  _7400 u_7400_8 (
    .pin1(n74138_1_pin7), .pin2(n7400_8_pin2), .pin3(n7400_8_pin3), .pin4(n7400_8_pin3), .pin5(n7400_8_pin5),
    .pin6(n7400_8_pin6), .pin13(n7400_8_pin13), .pin12(n74138_1_pin7), .pin11(n7400_8_pin11),
    .pin10(n7400_8_pin11), .pin9(dipswitch_2_sw1), .pin8(n7400_8_pin5));
  _74377 u_74377_1 (
    .pin1(n74377_1_pin1), .pin2(n7400_1_pin2), .pin3(n7400_1_pin6), .pin4(n7400_2_pin6), .pin5(n7400_2_pin2),
    .pin6(n7400_3_pin2), .pin7(n7400_3_pin6), .pin8(n7400_4_pin6), .pin9(n7400_4_pin2), .pin19(n7400_8_pin2),
    .pin18(n7400_8_pin6), .pin17(n7400_7_pin6), .pin16(n7400_7_pin2), .pin15(n7400_6_pin2),
    .pin14(n7400_6_pin6), .pin13(n7400_5_pin6), .pin12(n7400_5_pin2), .pin11(button_1_out));
  // also tied to GND on the sheet: {n74138_1_pin4, n74377_1_pin1}
  // also tied to VCC on the sheet: {n74138_1_pin6, n7400_1_pin13, n7400_2_pin13, n7400_3_pin13, n7400_4_pin13, n7400_5_pin13, n7400_6_pin13, n7400_7_pin13, n7400_8_pin13}

  // Notes on the sheet:
  //   Selector
  //   1 for all
  //   Write Pulse
  //   Data In
  //   74x374
endmodule
